// Logisim project Add2.circ as structural Verilog: 2 circuits, main circuit main
module main (
  input  A1,
  input  B1,
  input  A0,
  input  B0,
  input  CIN,
  output COUT,
  output C1,
  output C0
);

  wire full_adder_2_cout;

  Full_Adder full_adder_1 (.A(A1), .B(B1), .COUT(COUT), .CIN(full_adder_2_cout), .SUM(C1));
  Full_Adder full_adder_2 (.A(A0), .B(B0), .COUT(full_adder_2_cout), .CIN(CIN), .SUM(C0));
endmodule

module Full_Adder (
  input  A,
  input  B,
  input  CIN,
  output COUT,
  output SUM
);

  wire and_1_out, and_2_out, and_3_out, xor_1_out;

  and and_1 (and_1_out, A, B, B, B);
  and and_2 (and_2_out, A, CIN);
  and and_3 (and_3_out, B, CIN);
  xor xor_1 (xor_1_out, B, CIN);
  or or_1 (COUT, and_1_out, and_2_out, and_3_out);
  xor xor_2 (SUM, A, xor_1_out);
endmodule
