// Logisim project Cycle3.circ as structural Verilog: 1 circuit, main circuit main
module main (
);

  wire not_1_out, not_2_out, not_3_out;

  not not_1 (not_1_out, not_3_out);
  not not_2 (not_2_out, not_1_out);
  not not_3 (not_3_out, not_2_out);
endmodule
