// Logisim project FullAdder.circ as structural Verilog: 1 circuit, main circuit Full Adder
module Full_Adder (
  input  A,
  input  B,
  input  CIN,
  output COUT,
  output SUM
);

  wire and_1_out, and_2_out, and_3_out;

  and and_1 (and_1_out, A, B);
  and and_2 (and_2_out, A, CIN);
  and and_3 (and_3_out, CIN, B);
  or or_1 (COUT, and_1_out, and_2_out, and_3_out);
  ExactlyOne xor_1 (.out(SUM), .in0(A), .in2(B), .in4(CIN));
endmodule
