// Logisim project HalfAdder.circ as structural Verilog: 1 circuit, main circuit Half Adder
module Half_Adder (
  input  A,
  input  B,
  output SUM,
  output COUT
);

  xor xor_1 (SUM, A, B);
  and and_1 (COUT, A, B);
endmodule
