// Logisim project Mux2.circ as structural Verilog: 1 circuit, main circuit Mux2
module Mux2 (
  input  I0,
  input  I1,
  input  S,
  output O
);

  wire and_1_out, and_2_out, not_1_out;

  and and_1 (and_1_out, I0, not_1_out);
  not not_1 (not_1_out, S);
  and and_2 (and_2_out, S, I1);
  or or_1 (O, and_1_out, and_2_out);
endmodule
