// Logisim project Mux4.circ as structural Verilog: 1 circuit, main circuit Mux4
module Mux4 (
  input  I0,
  input  I1,
  input  I2,
  input  I3,
  input  S0,
  input  S1,
  output O
);

  wire mux2_1_o, mux2_2_o;

  Mux2 mux2_1 (.I0(I0), .I1(I1), .S(S0), .O(mux2_1_o));
  Mux2 mux2_2 (.I0(I2), .I1(I3), .S(S0), .O(mux2_2_o));
  Mux2 mux2_3 (.I0(mux2_1_o), .I1(mux2_2_o), .S(S1), .O(O));
endmodule
