// Logisim project DFF.circ as structural Verilog: 1 circuit, main circuit main
// DFF
module main (
  input  D,
  output Q,
  output nQ
);

  wire clock_1_out;

  Clock clock_1 (.out(clock_1_out));
  D_Flip_Flop d_ff_1 (.clk(clock_1_out), .D(D), .Q(Q), .Qn(nQ));  // open: preset, en, reset
endmodule
