// Logisim project SRFF.circ as structural Verilog: 1 circuit, main circuit main
module main (
  output Q,
  output nQ
);

  wire not_1_out, not_2_out, R_out, S_out;

  Button S (.out(S_out));
  Button R (.out(R_out));
  not not_1 (not_1_out, S_out);
  not not_2 (not_2_out, R_out);
  nand nand_1 (Q, not_1_out, nQ);
  nand nand_2 (nQ, Q, not_2_out);
endmodule
