// Logisim project TFF.circ as structural Verilog: 1 circuit, main circuit main
// DFF
module main (
  output Q,
  output nQ
);

  wire clock_1_out;

  Clock clock_1 (.out(clock_1_out));
  D_Flip_Flop d_ff_1 (.clk(clock_1_out), .D(nQ), .Q(Q), .Qn(nQ));  // open: preset, en, reset
endmodule
