// Logisim project RAM4.circ as structural Verilog: 1 circuit, main circuit Mux4
module Mux4 (
  input  WDATA,
  input  WE,
  input  WADDR_0,
  input  WADDR_0_2,
  input  RADDR_0,
  input  RADDR_1,
  output RDATA
);

  wire and_1_out, and_2_out, and_3_out, and_4_out, clock_1_out, d_ff_1_q, d_ff_2_q, d_ff_3_q, d_ff_4_q,
       decoder_1_out0, decoder_1_out1, decoder_1_out2, decoder_1_out3, mux2_1_o, mux2_2_o;

  Clock clock_1 (.out(clock_1_out));
  Decoder #(.select(2)) decoder_1 (
    .out0(decoder_1_out0), .out1(decoder_1_out1), .out2(decoder_1_out2), .out3(decoder_1_out3),
    .sel({WADDR_0, WADDR_0_2}));  // open: en
  and and_1 (and_1_out, decoder_1_out0, WE);
  and and_2 (and_2_out, decoder_1_out1, WE);
  and and_3 (and_3_out, decoder_1_out2, WE);
  and and_4 (and_4_out, decoder_1_out3, WE);
  D_Flip_Flop d_ff_1 (.clk(clock_1_out), .D(WDATA), .Q(d_ff_1_q), .en(and_1_out));  // open: Qn, preset, reset
  D_Flip_Flop d_ff_2 (.clk(clock_1_out), .D(WDATA), .Q(d_ff_2_q), .en(and_2_out));  // open: Qn, preset, reset
  D_Flip_Flop d_ff_3 (.clk(clock_1_out), .D(WDATA), .Q(d_ff_3_q), .en(and_3_out));  // open: Qn, preset, reset
  D_Flip_Flop d_ff_4 (.clk(clock_1_out), .D(WDATA), .Q(d_ff_4_q), .en(and_4_out));  // open: Qn, preset, reset
  Mux2 mux2_1 (.I0(d_ff_1_q), .I1(d_ff_2_q), .S(RADDR_0), .O(mux2_1_o));
  Mux2 mux2_2 (.I0(d_ff_3_q), .I1(d_ff_4_q), .S(RADDR_0), .O(mux2_2_o));
  Mux2 mux2_3 (.I0(mux2_1_o), .I1(mux2_2_o), .S(RADDR_1), .O(RDATA));
endmodule
