// Logisim project ROM4.circ as structural Verilog: 1 circuit, main circuit Mux4
module Mux4 (
  input  D_0,
  input  D_1,
  input  D_2,
  input  D_3,
  input  RADDR_0,
  input  RADDR_1,
  output RDATA
);

  wire mux2_1_o, mux2_2_o;

  Mux2 mux2_1 (.I0(D_0), .I1(D_1), .S(RADDR_0), .O(mux2_1_o));
  Mux2 mux2_2 (.I0(D_2), .I1(D_3), .S(RADDR_0), .O(mux2_2_o));
  Mux2 mux2_3 (.I0(mux2_1_o), .I1(mux2_2_o), .S(RADDR_1), .O(RDATA));
endmodule
